# Fritzing sketch Connecting XBee Shield to FEZ Panda-II (saved by Fritzing 0.7.0b)

parts:
  FEZ_Panda_II1 = FEZ Panda II
  Part1 = XBee Explorer Regulated
  U1 = XBee

nets:
  GND: FEZ_Panda_II1.GND, Part1.GND, U1.GND
  5V: FEZ_Panda_II1.5V, Part1.5V, U1.pin11
  N1: FEZ_Panda_II1.Di0, Part1.DOUT, U1.pin2
  N2: FEZ_Panda_II1.Di1, Part1.DIN, U1.pin3
  N3: Part1.DTR, U1.pin9
  N4: Part1.RES1, U1.pin8
  N5: Part1.DIO11, U1.pin7
  N6: Part1.RSSI, U1.pin6
  N7: Part1.RESET, U1.pin5
  N8: Part1.DIO12, U1.pin4
  3.3V: Part1.3.3V, U1.VCC
  N9: Part1.DIO1, U1.pin20
  N10: Part1.DIO2, U1.pin19
  N11: Part1.DIO3, U1.pin18
  N12: Part1.RTS, U1.pin17
  N13: Part1.DIO5, U1.pin16
  N14: Part1.RES2, U1.pin15
  N15: Part1.DIO9, U1.pin14
  N16: Part1.CTS, U1.pin13
  N17: Part1.DIO4, U1.pin12

custom parts:
  FEZ Panda II: FEZ Panda II is a tiny open-source board running Microsoft .NET Micro Framework.
