# Fritzing sketch Omnicopter Shield (saved by Fritzing 0.7.0b)
perfboards: 1

parts:
  FEZ_Panda_II3 = FEZ Panda II  # not connected
  J1 = female pin header, 2 pins [form="♀ (female)"]
  J2 = female pin header, 2 pins [form="♀ (female)"]  # not connected
  J3 = female pin header, 2 pins [form="♀ (female)"]  # not connected
  J4 = female pin header, 2 pins [form="♀ (female)"]
  J5 = female pin header, 2 pins [form="♀ (female)"]
  J6 = female pin header, 2 pins [form="♀ (female)"]
  J7 = female pin header, 2 pins [form="♀ (female)"]  # not connected
  J8 = female pin header, 2 pins [form="♀ (female)"]
  J9 = female pin header, 2 pins [form="♀ (female)"]
  J10 = female pin header, 2 pins [form="♀ (female)"]
  J11 = female pin header, 2 pins [form="♀ (female)"]
  J12 = female pin header, 2 pins [form="♀ (female)"]  # not connected
  J13 = female pin header, 2 pins [form="♀ (female)"]  # not connected
  J14 = female pin header, 2 pins [form="♀ (female)"]  # not connected
  J15 = female pin header, 2 pins [form="♀ (female)"]
  J16 = female pin header, 2 pins [form="♀ (female)"]  # not connected
  J17 = female pin header, 1 pin [form="♀ (female)"]
  J18 = female pin header, 2 pins [form="♀ (female)"]
  J19 = female pin header, 2 pins [form="♀ (female)"]  # not connected
  J20 = female pin header, 2 pins [form="♀ (female)"]
  J21 = female pin header, 2 pins [form="♀ (female)"]
  J22 = female pin header, 2 pins [form="♀ (female)"]
  J23 = female pin header, 2 pins [form="♀ (female)"]
  J24 = female pin header, 2 pins [form="♀ (female)"]
  J25 = female pin header, 2 pins [form="♀ (female)"]
  J26 = female pin header, 1 pin [form="♀ (female)"]
  J27 = female pin header, 1 pin [form="♀ (female)"]
  J28 = female pin header, 1 pin [form="♀ (female)"]
  J29 = female pin header, 1 pin [form="♀ (female)"]
  J30 = female pin header, 1 pin [form="♀ (female)"]
  J31 = female pin header, 1 pin [form="♀ (female)"]  # not connected
  J32 = female pin header, 1 pin [form="♀ (female)"]
  J33 = female pin header, 1 pin [form="♀ (female)"]

nets:
  N1: J1.pin2, J32.pin1
  N2: J4.pin1, J30.pin1
  N3: J4.pin2, J27.pin1
  N4: J5.pin2, J28.pin1
  N5: J6.pin1, J33.pin1
  N6: J8.pin1, J20.pin2
  N7: J8.pin2, J20.pin1
  N8: J9.pin1, J22.pin2
  N9: J9.pin2, J24.pin1
  N10: J10.pin2, J11.pin1, J21.pin2, J23.pin1
  N11: J15.pin2, J29.pin1
  N12: J17.pin1, J26.pin1
  N13: J18.pin1, J25.pin1
  N14: J18.pin2, J24.pin2

custom parts:
  FEZ Panda II: FEZ Panda II is a tiny open-source board running Microsoft .NET Micro Framework.
