# Fritzing sketch Power Distribution (saved by Fritzing 0.6.2b)
breadboards: 1

parts:
  VCC1 = obsolete Battery
  VCC2 = obsolete Battery
  J1 = Basic Servo
  J2 = Basic Servo
  J3 = Basic Servo
  J4 = Basic Servo
  J5 = Basic Servo
  J6 = Basic Servo
  J7 = Basic Servo
  J8 = Basic Servo

nets:
  VCC: VCC1.-, VCC2.+, J1.vcc, J2.vcc, J3.vcc, J4.vcc, J5.vcc, J6.vcc, J7.vcc, J8.vcc
  GND: VCC1.+, VCC2.-, J1.gnd, J2.gnd, J3.gnd, J4.gnd, J5.gnd, J6.gnd, J7.gnd, J8.gnd
